// Logisim project Nawal Ayesha_1911301042 Project.circ as structural Verilog: 12 circuits, main circuit main
module main (
  input  in_1,
  input  in_2,
  input  in_3,
  input  in_4,
  input  in_5,
  input  in_6,
  input  in_7,
  input  [2:0] in_8,
  input  [2:0] in_9,
  input  [2:0] in_10,
  input  in_11,
  input  in_12,
  output [12:0] out_13,
  output [12:0] out_14,
  output [12:0] out_15
);

  wire [2:0] alu_control_2_1_out_5;

  Register_file register_file_1 (
    .CLK(in_11), .Read_data_1(out_13), .Read_register_1__rs(in_8), .Read_data_2(out_14),
    .Write_Register(in_10), .Read_register_2__rt(in_9), .RegWrite(in_12), .WriteData(out_15));
  ALU_Control_2 alu_control_2_1 (.out_5(alu_control_2_1_out_5), .B(in_1), .A(in_2), .F1(in_3), .F0(in_4));
  _13_bit_ALU u_13_bit_alu_1 (
    .C_in(in_5), .B_inv(in_7), .A_inv(in_6), .A(out_13), .B(out_14), .Result(out_15),
    .ALU_Op(alu_control_2_1_out_5));  // open: Zero_Flag, Carry_Out, Overflow
endmodule

module _1_bit_ALU (
  input  [2:0] AluOp,
  input  A_invert,
  input  B_invert,
  input  C_in,
  input  A,
  input  B,
  output Result,
  output Carry_Out
);

  wire adder_1_out, and_1_out, multiplexer_1_out, multiplexer_2_out, not_1_out, not_2_out, or_1_out;

  not not_1 (not_1_out, A);
  not not_2 (not_2_out, B);
  Multiplexer #(.enable("false")) multiplexer_1 (.in0(A), .in1(not_1_out), .out(multiplexer_1_out), .sel(A_invert));
  Multiplexer #(.enable("false")) multiplexer_2 (.in0(B), .in1(not_2_out), .out(multiplexer_2_out), .sel(B_invert));
  and and_1 (and_1_out, multiplexer_1_out, multiplexer_2_out);
  or or_1 (or_1_out, multiplexer_1_out, multiplexer_2_out);
  Adder #(.width(1)) adder_1 (
    .a(multiplexer_1_out), .b(multiplexer_2_out), .out(adder_1_out), .cin(C_in), .cout(Carry_Out));
  Multiplexer #(.select(3), .enable("false")) multiplexer_3 (
    .in0(and_1_out), .in1(or_1_out), .in2(adder_1_out), .in3(or_1_out), .in4(and_1_out), .in6(adder_1_out),
    .in7(and_1_out), .out(Result), .sel(AluOp));  // open: in5
endmodule

module _13_bit_Multiplier (
  input  [12:0] A,
  input  [12:0] B,
  output [12:0] Product_S,
  output Mult_zero_flag
);

  wire or_1_out;
  wire [7:5] n4_bit_multiplier_2_s;

  _4_bit_Multiplier u_4_bit_multiplier_1 (.A(A[3:0]), .B(B[3:0]), .S(Product_S[7:0]));
  _4_bit_Multiplier u_4_bit_multiplier_2 (.A(A[7:4]), .B(B[7:4]), .S({n4_bit_multiplier_2_s, Product_S[12:8]}));
  or or_1 (or_1_out, Product_S[0], Product_S[1], Product_S[2], Product_S[3], Product_S[4], Product_S[5], Product_S[6], Product_S[7], Product_S[8], Product_S[9], Product_S[10], Product_S[11], Product_S[12]);
  not not_1 (Mult_zero_flag, or_1_out);
endmodule

module _4_bit_Multiplier (
  input  [3:0] A,
  input  [3:0] B,
  output [7:0] S
);

  wire [2:0] and_2_out;
  wire [3:0] and_5_out, and_9_out, and_13_out;
  wire [3:1] adder_1_out, adder_2_out;
  wire [3:3] adder_1_cout, adder_2_cout;

  and and_1 (S[0], A[0], B[0]);
  and and_2 (and_2_out[0], A[0], B[1]);
  and and_3 (and_2_out[1], A[0], B[2]);
  and and_4 (and_2_out[2], A[0], B[3]);
  and and_5 (and_5_out[0], A[1], B[0]);
  and and_6 (and_5_out[1], A[1], B[1]);
  and and_7 (and_5_out[2], A[1], B[2]);
  and and_8 (and_5_out[3], A[1], B[3]);
  Adder #(.width(4)) adder_1 (
    .a({1'b0, and_2_out}), .b(and_5_out), .out({adder_1_out, S[1]}), .cin(1'b0), .cout(adder_1_cout[3]));
  and and_9 (and_9_out[0], A[2], B[0]);
  and and_10 (and_9_out[1], A[2], B[1]);
  and and_11 (and_9_out[2], A[2], B[2]);
  and and_12 (and_9_out[3], A[2], B[3]);
  Adder #(.width(4)) adder_2 (
    .a({adder_1_cout[3], adder_1_out}), .b(and_9_out), .out({adder_2_out, S[2]}), .cin(1'b0),
    .cout(adder_2_cout[3]));
  and and_13 (and_13_out[0], A[3], B[0]);
  and and_14 (and_13_out[1], A[3], B[1]);
  and and_15 (and_13_out[2], A[3], B[2]);
  and and_16 (and_13_out[3], A[3], B[3]);
  Adder #(.width(4)) adder_3 (
    .a({adder_2_cout[3], adder_2_out}), .b(and_13_out), .out(S[6:3]), .cin(1'b0), .cout(S[7]));

  // Notes on the sheet:
  //   A1B1
  //   A1B2
  //   A1B3
  //   A1B4
  //   A2B1
  //   A2B2
  //   A2B3
  //   A2B4
  //   A3B1
  //   A3B2
  //   A3B3
  //   A3B4
  //   A4B1
  //   A4B2
  //   A4B3
  //   A4B4
endmodule

module _13_bit_ALU (
  input  [2:0] ALU_Op,
  input  C_in,
  input  B_inv,
  input  A_inv,
  input  [12:0] A,
  input  [12:0] B,
  output [12:0] Result,
  output Zero_Flag,
  output Overflow,
  output Carry_Out
);

  wire n1_bit_alu_1_carry_out, n1_bit_alu_2_carry_out, n1_bit_alu_3_carry_out, n1_bit_alu_4_carry_out,
       n1_bit_alu_5_carry_out, n1_bit_alu_6_carry_out, n1_bit_alu_7_carry_out, n1_bit_alu_8_carry_out,
       n1_bit_alu_9_carry_out, n1_bit_alu_10_carry_out, n1_bit_alu_11_carry_out, n1_bit_alu_12_carry_out,
       n13_bit_multiplier_1_mult_zero_flag, not_1_out, or_1_out;
  wire [12:0] n1_bit_alu_1_result, n13_bit_multiplier_1_product_s;

  _1_bit_ALU u_1_bit_alu_1 (
    .Result(n1_bit_alu_1_result[0]), .Carry_Out(n1_bit_alu_1_carry_out), .A(A[0]), .B(B[0]),
    .A_invert(A_inv), .B_invert(B_inv), .AluOp(ALU_Op), .C_in(C_in));
  _1_bit_ALU u_1_bit_alu_2 (
    .Result(n1_bit_alu_1_result[1]), .Carry_Out(n1_bit_alu_2_carry_out), .A(A[1]), .B(B[1]),
    .A_invert(A_inv), .B_invert(B_inv), .AluOp(ALU_Op), .C_in(n1_bit_alu_1_carry_out));
  _1_bit_ALU u_1_bit_alu_3 (
    .Result(n1_bit_alu_1_result[2]), .Carry_Out(n1_bit_alu_3_carry_out), .A(A[2]), .B(B[2]),
    .A_invert(A_inv), .B_invert(B_inv), .AluOp(ALU_Op), .C_in(n1_bit_alu_2_carry_out));
  _1_bit_ALU u_1_bit_alu_4 (
    .Result(n1_bit_alu_1_result[3]), .Carry_Out(n1_bit_alu_4_carry_out), .A(A[3]), .B(B[3]),
    .A_invert(A_inv), .B_invert(B_inv), .AluOp(ALU_Op), .C_in(n1_bit_alu_3_carry_out));
  _1_bit_ALU u_1_bit_alu_5 (
    .Result(n1_bit_alu_1_result[4]), .Carry_Out(n1_bit_alu_5_carry_out), .A(A[4]), .B(B[4]),
    .A_invert(A_inv), .B_invert(B_inv), .AluOp(ALU_Op), .C_in(n1_bit_alu_4_carry_out));
  _1_bit_ALU u_1_bit_alu_6 (
    .Result(n1_bit_alu_1_result[5]), .Carry_Out(n1_bit_alu_6_carry_out), .A(A[5]), .B(B[5]),
    .A_invert(A_inv), .B_invert(B_inv), .AluOp(ALU_Op), .C_in(n1_bit_alu_5_carry_out));
  _1_bit_ALU u_1_bit_alu_7 (
    .Result(n1_bit_alu_1_result[6]), .Carry_Out(n1_bit_alu_7_carry_out), .A(A[6]), .B(B[6]),
    .A_invert(A_inv), .B_invert(B_inv), .AluOp(ALU_Op), .C_in(n1_bit_alu_6_carry_out));
  _1_bit_ALU u_1_bit_alu_8 (
    .Result(n1_bit_alu_1_result[7]), .Carry_Out(n1_bit_alu_8_carry_out), .A(A[7]), .B(B[7]),
    .A_invert(A_inv), .B_invert(B_inv), .AluOp(ALU_Op), .C_in(n1_bit_alu_7_carry_out));
  _1_bit_ALU u_1_bit_alu_9 (
    .Result(n1_bit_alu_1_result[8]), .Carry_Out(n1_bit_alu_9_carry_out), .A(A[8]), .B(B[8]),
    .A_invert(A_inv), .B_invert(B_inv), .AluOp(ALU_Op), .C_in(n1_bit_alu_8_carry_out));
  _1_bit_ALU u_1_bit_alu_10 (
    .Result(n1_bit_alu_1_result[9]), .Carry_Out(n1_bit_alu_10_carry_out), .A(A[9]), .B(B[9]),
    .A_invert(A_inv), .B_invert(B_inv), .AluOp(ALU_Op), .C_in(n1_bit_alu_9_carry_out));
  _1_bit_ALU u_1_bit_alu_11 (
    .Result(n1_bit_alu_1_result[10]), .Carry_Out(n1_bit_alu_11_carry_out), .A(A[10]), .B(B[10]),
    .A_invert(A_inv), .B_invert(B_inv), .AluOp(ALU_Op), .C_in(n1_bit_alu_10_carry_out));
  _1_bit_ALU u_1_bit_alu_12 (
    .Result(n1_bit_alu_1_result[11]), .Carry_Out(n1_bit_alu_12_carry_out), .A(A[11]), .B(B[11]),
    .A_invert(A_inv), .B_invert(B_inv), .AluOp(ALU_Op), .C_in(n1_bit_alu_11_carry_out));
  _1_bit_ALU u_1_bit_alu_13 (
    .Result(n1_bit_alu_1_result[12]), .Carry_Out(Carry_Out), .A(A[12]), .B(B[12]), .A_invert(A_inv),
    .B_invert(B_inv), .AluOp(ALU_Op), .C_in(n1_bit_alu_12_carry_out));
  _13_bit_Multiplier u_13_bit_multiplier_1 (
    .A(A), .B(B), .Product_S(n13_bit_multiplier_1_product_s),
    .Mult_zero_flag(n13_bit_multiplier_1_mult_zero_flag));
  Multiplexer #(.select(3), .width(13), .enable("false")) multiplexer_1 (
    .in0(n1_bit_alu_1_result), .in1(n1_bit_alu_1_result), .in2(n1_bit_alu_1_result),
    .in3(n1_bit_alu_1_result), .in4(n1_bit_alu_1_result), .in6(n1_bit_alu_1_result),
    .in7(n13_bit_multiplier_1_product_s), .out(Result), .sel(ALU_Op));  // open: in5
  or or_1 (or_1_out, n1_bit_alu_1_result[0], n1_bit_alu_1_result[1], n1_bit_alu_1_result[2], n1_bit_alu_1_result[3], n1_bit_alu_1_result[4], n1_bit_alu_1_result[5], n1_bit_alu_1_result[6], n1_bit_alu_1_result[7], n1_bit_alu_1_result[8], n1_bit_alu_1_result[9], n1_bit_alu_1_result[10], n1_bit_alu_1_result[11], n1_bit_alu_1_result[12]);
  xor xor_1 (Overflow, n1_bit_alu_12_carry_out, Carry_Out);
  not not_1 (not_1_out, or_1_out);
  Multiplexer #(.select(3), .enable("false")) multiplexer_2 (
    .in0(not_1_out), .in1(not_1_out), .in2(not_1_out), .in3(not_1_out), .in4(not_1_out), .in6(not_1_out),
    .in7(n13_bit_multiplier_1_mult_zero_flag), .out(Zero_Flag), .sel(ALU_Op));  // open: in5
endmodule

module ALU_Control_NOR (
  input  C,
  input  B_invert,
  input  A_invert,
  input  F1,
  input  F0,
  output [2:0] ALU_Op
);

  wire CB_prime_A_prime_F1_prime_F0__prime_2_out, CB_prime_A_prime_F1_prime_F0__prime_out,
       CB_prime_A_prime_F1_prime_F0_prime__prime_out, CB_prime_F1_prime_F0__prime_out,
       CBAF1_prime__prime_out, CBAF1_prime_F0_prime__prime_2_out, CBAF1_prime_F0_prime__prime_out,
       CBAF1F0__prime_out, nor_1_out, nor_2_out, nor_3_out, nor_4_out, nor_5_out, nor_6_out, nor_7_out;

  nor nor_1 (nor_1_out, B_invert, B_invert);
  nor nor_2 (nor_2_out, A_invert, A_invert);
  nor nor_3 (nor_3_out, F1, F1);
  nor nor_4 (nor_4_out, F0, F0);
  nor CBAF1_prime_F0_prime__prime (CBAF1_prime_F0_prime__prime_out, C, B_invert, A_invert, nor_3_out, nor_4_out);
  nor CB_prime_A_prime_F1_prime_F0__prime (CB_prime_A_prime_F1_prime_F0__prime_out, C, nor_1_out, nor_2_out, nor_3_out, nor_4_out);
  nor CB_prime_A_prime_F1_prime_F0_prime__prime (CB_prime_A_prime_F1_prime_F0_prime__prime_out, C, nor_1_out, A_invert, nor_3_out, F0);
  nor CBAF1F0__prime (CBAF1F0__prime_out, C, B_invert, F1, A_invert, F0);
  nor CBAF1_prime_F0_prime__prime_2 (CBAF1_prime_F0_prime__prime_2_out, C, B_invert, A_invert, nor_3_out, nor_4_out);
  nor CB_prime_F1_prime_F0__prime (CB_prime_F1_prime_F0__prime_out, C, nor_1_out, nor_3_out, F0);
  nor CBAF1_prime__prime (CBAF1_prime__prime_out, C, B_invert, A_invert, nor_3_out);
  nor CB_prime_A_prime_F1_prime_F0__prime_2 (CB_prime_A_prime_F1_prime_F0__prime_2_out, C, nor_1_out, nor_2_out, nor_3_out, F0);
  nor nor_5 (nor_5_out, CBAF1F0__prime_out, CBAF1_prime_F0_prime__prime_2_out, CB_prime_F1_prime_F0__prime_out);
  nor nor_6 (nor_6_out, CBAF1_prime__prime_out, CB_prime_A_prime_F1_prime_F0__prime_2_out);
  nor nor_7 (nor_7_out, CBAF1_prime_F0_prime__prime_out, CB_prime_A_prime_F1_prime_F0__prime_out, CB_prime_A_prime_F1_prime_F0_prime__prime_out);
  nor y (ALU_Op[1], nor_5_out, nor_5_out);
  nor z (ALU_Op[0], nor_6_out, nor_6_out);
  nor x (ALU_Op[2], nor_7_out, nor_7_out);
endmodule

module Part_1 (
  input  C,
  input  B,
  input  A,
  input  F1,
  input  F0,
  input  C_In,
  input  [12:0] A_2,
  input  [12:0] B_2,
  output [2:0] out_9,
  output out_10,
  output [12:0] out_11,
  output out_12,
  output out_13
);

  ALU_Control_NOR alu_control_nor_1 (.ALU_Op(out_9), .C(C), .B_invert(B), .A_invert(A), .F1(F1), .F0(F0));
  _13_bit_ALU u_13_bit_alu_1 (
    .C_in(C_In), .B_inv(B), .A_inv(A), .A(A_2), .B(B_2), .Result(out_11), .Zero_Flag(out_10), .ALU_Op(out_9),
    .Carry_Out(out_13), .Overflow(out_12));
endmodule

module Instruction_Fetch (
  input  CLK,
  input  CLR,
  output [1:0] Op,
  output [2:0] rs,
  output [2:0] rt,
  output [2:0] rd,
  output [1:0] funct
);

  wire [12:0] adder_1_out, register_1_q;

  Register #(.width(13)) register_1 (.D(adder_1_out), .en(1'b1), .Q(register_1_q), .clk(CLK), .clr(CLR));
  ROM #(.addrWidth(13), .dataWidth(13)) rom_1 (.addr(register_1_q), .data({Op, rs, rt, rd, funct}));  // open: sel
  Adder #(.width(13)) adder_1 (.a(13'h1), .b(register_1_q), .out(adder_1_out), .cin(1'b0));  // open: cout

  // Notes on the sheet:
  //   PC
  //   Address
  //   contents of rom_1 (hex, n*v repeats v):
  //   408 288 890 14b a94 110 1d1 111 11 10 43 1001 1010 1011 1110 101
  //   Instruction
endmodule

module Register_file (
  input  CLK,
  input  [2:0] Read_register_1__rs,
  input  [2:0] Write_Register,
  input  [2:0] Read_register_2__rt,
  input  RegWrite,
  input  [12:0] WriteData,
  output [12:0] Read_data_1,
  output [12:0] Read_data_2
);

  wire and_1_out, and_2_out, and_3_out, and_4_out, and_5_out, and_6_out, and_7_out, and_8_out,
       decoder_1_out0, decoder_1_out1, decoder_1_out2, decoder_1_out3, decoder_1_out4, decoder_1_out5,
       decoder_1_out6, decoder_1_out7;
  wire [12:0] _0_q, _1_q, _2_q, _3_q, _4_q, _5_q, _6_q, _7_q;

  Decoder #(.select(3), .enable("false")) decoder_1 (
    .out0(decoder_1_out0), .out1(decoder_1_out1), .out2(decoder_1_out2), .out3(decoder_1_out3),
    .out4(decoder_1_out4), .out5(decoder_1_out5), .out6(decoder_1_out6), .out7(decoder_1_out7),
    .sel(Write_Register));
  and and_1 (and_1_out, decoder_1_out0, RegWrite);
  and and_2 (and_2_out, decoder_1_out1, RegWrite);
  and and_3 (and_3_out, decoder_1_out2, RegWrite);
  and and_4 (and_4_out, decoder_1_out3, RegWrite);
  and and_5 (and_5_out, decoder_1_out4, RegWrite);
  and and_6 (and_6_out, decoder_1_out5, RegWrite);
  and and_7 (and_7_out, decoder_1_out6, RegWrite);
  and and_8 (and_8_out, decoder_1_out7, RegWrite);
  Register #(.width(13)) _0 (.D(WriteData), .en(and_1_out), .Q(_0_q), .clk(CLK));  // open: clr
  Register #(.width(13)) _1 (.D(WriteData), .en(and_2_out), .Q(_1_q), .clk(CLK));  // open: clr
  Register #(.width(13)) _2 (.D(WriteData), .en(and_3_out), .Q(_2_q), .clk(CLK));  // open: clr
  Register #(.width(13)) _3 (.D(WriteData), .en(and_4_out), .Q(_3_q), .clk(CLK));  // open: clr
  Register #(.width(13)) _4 (.D(WriteData), .en(and_5_out), .Q(_4_q), .clk(CLK));  // open: clr
  Register #(.width(13)) _5 (.D(WriteData), .en(and_6_out), .Q(_5_q), .clk(CLK));  // open: clr
  Register #(.width(13)) _6 (.D(WriteData), .en(and_7_out), .Q(_6_q), .clk(CLK));  // open: clr
  Register #(.width(13)) _7 (.D(WriteData), .en(and_8_out), .Q(_7_q), .clk(CLK));  // open: clr
  Multiplexer #(.select(3), .width(13), .enable("false")) multiplexer_1 (
    .in0(_0_q), .in1(_1_q), .in2(_2_q), .in3(_3_q), .in4(_4_q), .in5(_5_q), .in6(_6_q), .in7(_7_q),
    .out(Read_data_1), .sel(Read_register_1__rs));
  Multiplexer #(.select(3), .width(13), .enable("false")) multiplexer_2 (
    .in0(_0_q), .in1(_1_q), .in2(_2_q), .in3(_3_q), .in4(_4_q), .in5(_5_q), .in6(_6_q), .in7(_7_q),
    .out(Read_data_2), .sel(Read_register_2__rt));
endmodule

module Instruction_Control (
  input  [1:0] Opcode,
  output RegDst,
  output ALUSrc,
  output MemtoReg,
  output RegWrite,
  output MemRead,
  output MemWrite,
  output Branch,
  output ALUOp0,
  output ALUOp1
);

  wire not_1_out, not_2_out;

  not not_1 (not_1_out, Opcode[0]);
  not not_2 (not_2_out, Opcode[1]);
  and and_1 (ALUOp0, not_1_out, not_2_out);
  and and_2 (MemRead, not_2_out, Opcode[0]);
  and and_3 (MemWrite, not_1_out, Opcode[1]);
  and and_4 (ALUOp1, Opcode[0], Opcode[1]);
  or or_1 (ALUSrc, MemRead, MemWrite);
  or or_2 (RegWrite, ALUOp0, MemRead);

  assign Branch = ALUOp1;
  assign MemtoReg = MemRead;
  assign RegDst = ALUOp0;

  // Notes on the sheet:
  //   R-Format
  //   lw
  //   sw
  //   beq
endmodule

module Mid_Q3 (
  input  in_1,
  input  in_2,
  input  in_3,
  input  CLK,
  input  CLR,
  output [1:0] out_6,
  output [12:0] out_7,
  output [2:0] rs,
  output [12:0] out_9,
  output [2:0] out_10,
  output [12:0] out_11,
  output [2:0] rt,
  output [2:0] out_13,
  output [1:0] funct,
  output [2:0] out_15,
  output [12:0] out_16
);

  wire beq_out, instruction_control_1_aluop0, instruction_control_1_aluop1, instruction_control_1_alusrc,
       instruction_control_1_branch, instruction_control_1_memread, instruction_control_1_memtoreg,
       instruction_control_1_memwrite, instruction_control_1_regdst, instruction_control_1_regwrite,
       n13_bit_alu_1_zero_flag;
  wire [12:0] adder_1_out, adder_2_out, multiplexer_3_out, ram_1_data, register_1_q, register_file_1_p7,
       register_file_1_p8, shifter_1_out;

  Multiplexer #(.width(13), .enable("false")) multiplexer_1 (
    .in0(adder_1_out), .in1(adder_2_out), .out(out_7), .sel(beq_out));
  Register #(.width(13)) register_1 (.D(out_7), .en(1'b1), .Q(register_1_q), .clk(CLK), .clr(CLR));
  ROM #(.addrWidth(13), .dataWidth(13)) rom_1 (
    .addr(register_1_q), .data({out_6, rs, out_10, rt, funct}));  // open: sel
  Adder #(.width(13)) adder_1 (.a(13'h1), .b(register_1_q), .out(adder_1_out), .cin(1'b0));  // open: cout
  Multiplexer #(.width(3), .enable("false")) multiplexer_2 (
    .in0(out_10), .in1(rt), .out(out_13), .sel(instruction_control_1_regdst));
  assign out_16 = {{8{1'b0}}, {rt, funct}};  // Bit_Extender bit_extender_1
  Instruction_Control instruction_control_1 (
    .Opcode(out_6), .RegDst(instruction_control_1_regdst), .ALUSrc(instruction_control_1_alusrc),
    .MemtoReg(instruction_control_1_memtoreg), .RegWrite(instruction_control_1_regwrite),
    .MemRead(instruction_control_1_memread), .MemWrite(instruction_control_1_memwrite),
    .Branch(instruction_control_1_branch), .ALUOp0(instruction_control_1_aluop0),
    .ALUOp1(instruction_control_1_aluop1));
  // Register_file register_file_1: pin names not known; wires that end beside it: rs, out_10, out_13, out_9, CLK, instruction_control_1_regwrite, register_file_1_p7, register_file_1_p8
  Multiplexer #(.width(13), .enable("false")) multiplexer_3 (
    .in0(register_file_1_p8), .in1(out_16), .out(multiplexer_3_out), .sel(instruction_control_1_alusrc));
  Shifter #(.width(13)) shifter_1 (.in(out_16), .\dist (4'b0010), .out(shifter_1_out));
  Adder #(.width(13)) adder_2 (.a(adder_1_out), .b(shifter_1_out), .out(adder_2_out), .cin(1'b0));  // open: cout
  _13_bit_ALU u_13_bit_alu_1 (
    .C_in(in_3), .B_inv(in_2), .A_inv(in_1), .A(register_file_1_p7), .B(multiplexer_3_out), .Result(out_11),
    .Zero_Flag(n13_bit_alu_1_zero_flag), .ALU_Op(out_15));  // open: Carry_Out, Overflow
  ALU_Control_2 alu_control_2_1 (
    .out_5(out_15), .B(instruction_control_1_aluop0), .A(instruction_control_1_aluop1), .F1(funct[1]),
    .F0(funct[0]));
  and beq (beq_out, instruction_control_1_branch, n13_bit_alu_1_zero_flag);
  RAM #(.addrWidth(13), .dataWidth(13), .bus("separate")) ram_1 (
    .addr(out_11), .din(register_file_1_p8), .data(ram_1_data), .str(instruction_control_1_memwrite),
    .clk(CLK), .ld(instruction_control_1_memread));  // open: sel, clr
  Multiplexer #(.width(13), .enable("false")) multiplexer_4 (
    .in0(out_11), .in1(ram_1_data), .out(out_9), .sel(instruction_control_1_memtoreg));

  // Notes on the sheet:
  //   PCSrc
  //   PC
  //   Address
  //   contents of rom_1 (hex, n*v repeats v):
  //   800 4 8 1900 228 1044 3f4 1a10 11 10 43 1001 1010 1011 1110 101
  //   Instruction
  //   op
  //   rd
  //   funct
endmodule

module ALU_Control_2 (
  input  B,
  input  A,
  input  F1,
  input  F0,
  output [2:0] out_5
);

  wire not_1_out, not_2_out;

  not not_1 (not_1_out, A);
  not not_2 (not_2_out, F0);
  and and_1 (out_5[2], not_2_out, F1, not_1_out, B);
  and and_2 (out_5[1], B, not_1_out, not_2_out);
  and and_3 (out_5[0], F0, F1, not_1_out, B);
endmodule
